// Logisim project MIPS32.circ as structural Verilog
module Fetch (
);

  wire clock_1_out;
  wire [1:0] incrementer_1_p3;
  wire [29:0] incrementer_1_p1, incrementer_1_p2;

  Clock clock_1 (.out(clock_1_out));
  // Incrementer #(.width(30)) incrementer_1: pin names not known; wires that end beside it: incrementer_1_p1, incrementer_1_p2, {incrementer_1_p1, incrementer_1_p3}
  Register #(.width(32)) register_1 (
    .D({incrementer_1_p2, incrementer_1_p3}), .en(clock_1_out), .clk(clock_1_out),
    .Q({incrementer_1_p1, incrementer_1_p3}));  // open: clr
  // MIPSProgramROM mipsprogramrom_1: pin names not known

  // Notes on the sheet:
  //   contents of mipsprogramrom_1 (hex, n*v repeats v):
  //   ADDIU $t2, $zero, 1 ADDU $v0, $t1, $t2 ADDU $t1, $zero, $t2 ADDU $t2, $zero, $v0 ADDU $v0, $t1, $t2
  //   ADDU $t1, $zero, $t2 ADDU $t2, $zero, $v0 ADDU $v0, $t1, $t2 ADDU $t1, $zero, $t2 ADDU $t2, $zero,
  //   $v0
endmodule

module Decode (
  input  [31:0] Word,
  output [31:0] A,
  output [31:0] LUI_Data,
  output [31:0] B,
  output [4:0] Sa,
  output [31:0] Ctrl,
  output LUI,
  output [3:0] Op_ALU,
  output SLT,
  output SLTU
);

  wire [4:0] multiplexer_1_out, multiplexer_2_out;
  wire [31:0] bit_extender_2_out, bit_extender_3_out, multiplexer_4_out, registerfile_1_p5;

  assign LUI_Data[15:0] = {{15{Word[30]}}, Word[30]};  // Bit_Extender bit_extender_1
  Multiplexer #(.width(5), .enable("false")) multiplexer_1 (
    .in0(Word[15:11]), .in1(Word[20:16]), .out(multiplexer_1_out), .sel(Word[29]));
  assign bit_extender_2_out = {{16{Word[15]}}, Word[15:0]};  // Bit_Extender bit_extender_2
  assign bit_extender_3_out = {{16{1'b0}}, Word[15:0]};  // Bit_Extender bit_extender_3
  Multiplexer #(.width(5), .enable("false")) multiplexer_2 (
    .in0(multiplexer_1_out), .in1(Word[20:16]), .out(multiplexer_2_out), .sel(Word[31]));
  Controls controls_1 (.Opcode(Word[31:26]), .Funct(Word[5:0]), .LUI(LUI), .Op_ALU(Op_ALU), .SLT(SLT), .SLTU(SLTU));
  // RegisterFile registerfile_1: pin names not known; wires that end beside it: multiplexer_2_out, Word[25:21], Word[20:16], A, registerfile_1_p5
  Multiplexer #(.width(32), .enable("false")) multiplexer_3 (
    .in0(registerfile_1_p5), .in1(multiplexer_4_out), .out(B), .sel(Word[29]));
  Multiplexer #(.width(32), .enable("false")) multiplexer_4 (
    .in0(bit_extender_2_out), .in1(bit_extender_3_out), .out(multiplexer_4_out), .sel(Word[28]));

  assign Ctrl = Word;
  assign LUI_Data[31:16] = Word[15:0];
  assign Sa = Word[10:6];
endmodule

module Controls (
  input  [5:0] Opcode,
  input  [5:0] Funct,
  output LUI,
  output [3:0] Op_ALU,
  output SLT,
  output SLTU
);

  wire and_1_out, and_2_out, and_4_out, and_5_out, and_6_out, not_1_out, not_4_out;
  wire [3:0] multiplexer_1_out;
  wire [3:1] not_2_out;

  and and_1 (and_1_out, Funct[3], Funct[0], Funct[1]);
  not not_1 (not_1_out, Funct[2]);
  and and_2 (and_2_out, not_1_out, Funct[3]);
  not not_2 (not_2_out[1], Funct[4]);
  not not_3 (not_2_out[3], Funct[4]);
  and and_3 (LUI, Opcode[0], Opcode[1], Opcode[2]);
  not not_4 (not_4_out, Opcode[2]);
  and and_4 (and_4_out, Opcode[1], not_4_out);
  Multiplexer #(.width(4), .enable("false")) multiplexer_1 (
    .in0({Funct[2:0], Funct[5]}), .in1({not_2_out[3], Funct[4], not_2_out[1], Funct[4]}),
    .out(multiplexer_1_out), .sel(and_1_out));
  Multiplexer #(.width(4), .enable("false")) multiplexer_2 (
    .in0({Opcode[2:0], Opcode[5]}), .in1(multiplexer_1_out), .out(Op_ALU), .sel(Opcode[3]));
  or or_1 (SLT, and_4_out, and_2_out);
  and and_5 (and_5_out, and_4_out, Opcode[0]);
  and and_6 (and_6_out, Funct[0], and_2_out);
  or or_2 (SLTU, and_5_out, and_6_out);

  // Notes on the sheet:
  //   Arith
endmodule

module Execute (
  input  [31:0] A,
  input  [31:0] B,
  input  [31:0] LUI_Data,
  input  [31:0] Word,
  input  LUI,
  input  SLT,
  input  [3:0] Op_ALU,
  input  [4:0] Sa,
  input  SLTU
);

  wire and_1_out, and_2_out, comparator_1_eq, comparator_1_lt, comparator_2_eq, comparator_2_lt,
       multiplexer_2_out, not_1_out, not_2_out;
  wire [31:0] bit_extender_1_out, mips_alu_1_p5, multiplexer_1_out, multiplexer_3_out;

  // Mips_ALU mips_alu_1: pin names not known; wires that end beside it: A, B, Op_ALU, Sa, mips_alu_1_p5
  Comparator #(.width(32)) comparator_1 (.a(A), .b(B), .eq(comparator_1_eq), .lt(comparator_1_lt));  // open: gt
  Comparator #(.width(32), .mode("unsigned")) comparator_2 (
    .a(A), .b(B), .eq(comparator_2_eq), .lt(comparator_2_lt));  // open: gt
  not not_1 (not_1_out, comparator_1_eq);
  not not_2 (not_2_out, comparator_2_eq);
  Multiplexer #(.width(32), .enable("false")) multiplexer_1 (
    .in0(mips_alu_1_p5), .in1(LUI_Data), .out(multiplexer_1_out), .sel(LUI));
  and and_1 (and_1_out, not_1_out, comparator_1_lt);
  and and_2 (and_2_out, not_2_out, comparator_2_lt);
  Multiplexer #(.enable("false")) multiplexer_2 (.in0(and_1_out), .in1(and_2_out), .out(multiplexer_2_out), .sel(SLTU));
  Multiplexer #(.width(32), .enable("false")) multiplexer_3 (
    .in0(multiplexer_1_out), .in1(bit_extender_1_out), .out(multiplexer_3_out), .sel(SLT));
  assign bit_extender_1_out = {{31{multiplexer_2_out}}, multiplexer_2_out};  // Bit_Extender bit_extender_1

  // Notes on the sheet:
  //   SLT
  //   SLTU
endmodule
