// Logisim project MIPS32.circ as structural Verilog: 13 circuits, main circuit MIPS32
module MIPS32 (
  output [31:0] out_1,
  output [31:0] out_2,
  output [31:0] out_3,
  output [31:0] out_4,
  output [31:0] out_5,
  output [4:0] out_6,
  output [31:0] out_7,
  output [4:0] out_8,
  output [4:0] out_9,
  output [31:0] out_10,
  output [31:0] out_11
);

  wire clock_1_out, decode_1_lui_out, decode_1_slt_out, decode_1_sltu_out, decode_1_we, ex_mem_1_we_out,
       execute_1_we_out, id_ex_1_lui_out, id_ex_1_slt_out, id_ex_1_sltu_out, id_ex_1_we_out, mem_wb_1_we_out,
       memory_1_we_out, writeback_1_we_out;
  wire [3:0] decode_1_op_alu_out, id_ex_1_op_alu_out;
  wire [4:0] decode_1_ra, decode_1_rb, decode_1_rw, decode_1_sa_out, execute_1_rw_out, id_ex_1_ra_out,
       id_ex_1_rb_out, id_ex_1_rw_out, id_ex_1_sa_out, writeback_1_rw_out;
  wire [31:0] decode_1_ctrl_out, decode_1_lui_data_out, ex_mem_1_word_out, execute_1_word_out,
       forwarding_1_a_out, forwarding_1_b_out, id_ex_1_ctrl_out, id_ex_1_lui_data_out, if_id_1_word_out,
       mem_wb_1_c_out, mem_wb_1_data_out, memory_1_c_out, memory_1_data;

  Clock clock_1 (.out(clock_1_out));
  Fetch fetch_1 (.CLK(clock_1_out), .Word(out_10));
  IF_ID if_id_1 (.Word_in(out_10), .CLK(clock_1_out), .Word_out(if_id_1_word_out));
  Decode decode_1 (
    .C_In(out_1), .CLK(clock_1_out), .WE_in(writeback_1_we_out), .Word(if_id_1_word_out),
    .rW_in(writeback_1_rw_out), .Aout(out_2), .LUI_Data_out(decode_1_lui_data_out), .B_out(out_5),
    .Sa_out(decode_1_sa_out), .Ctrl_out(decode_1_ctrl_out), .WE(decode_1_we), .LUI_out(decode_1_lui_out),
    .Op_ALU_out(decode_1_op_alu_out), .SLT_out(decode_1_slt_out), .SLTU_out(decode_1_sltu_out),
    .rW(decode_1_rw), .rA(decode_1_ra), .rB(decode_1_rb));
  ID_EX id_ex_1 (
    .A_in(out_2), .LUI_Data_in(decode_1_lui_data_out), .B_in(out_5), .CLK(clock_1_out),
    .Sa_in(decode_1_sa_out), .SLT_in(decode_1_slt_out), .SLTU_in(decode_1_sltu_out),
    .LUI_in(decode_1_lui_out), .Ctrl_in(decode_1_ctrl_out), .Op_ALU_in(decode_1_op_alu_out),
    .rW_in(decode_1_rw), .rA(decode_1_ra), .rB(decode_1_rb), .WE(decode_1_we), .A_out(out_3),
    .LUI_Data_out(id_ex_1_lui_data_out), .B_out(out_7), .Sa_out(id_ex_1_sa_out), .SLT_out(id_ex_1_slt_out),
    .SLTU_out(id_ex_1_sltu_out), .LUI_out(id_ex_1_lui_out), .Ctrl_out(id_ex_1_ctrl_out),
    .Op_ALU_out(id_ex_1_op_alu_out), .rW_out(id_ex_1_rw_out), .rA_out(id_ex_1_ra_out),
    .rB_out(id_ex_1_rb_out), .WE_out(id_ex_1_we_out));
  Execute execute_1 (
    .A(forwarding_1_a_out), .B(forwarding_1_b_out), .LUI_Data(id_ex_1_lui_data_out), .LUI(id_ex_1_lui_out),
    .SLT(id_ex_1_slt_out), .Op_ALU(id_ex_1_op_alu_out), .Sa(id_ex_1_sa_out), .SLTU(id_ex_1_sltu_out),
    .Word_in(id_ex_1_ctrl_out), .rW(id_ex_1_rw_out), .WE_in(id_ex_1_we_out), .C(out_4),
    .Word_out(execute_1_word_out), .rW_out(execute_1_rw_out), .WE_out(execute_1_we_out));
  Forwarding forwarding_1 (
    .ID_EX_A(out_3), .ID_EX_B(out_7), .EX_MEM_Out(out_11), .MEM_WB_Out(mem_wb_1_c_out), .rA(id_ex_1_ra_out),
    .rB(id_ex_1_rb_out), .rD_EX_MEM(out_6), .rD_MEM_WB(out_8), .WE_EX_MEM(ex_mem_1_we_out),
    .WE_MEM_WB(mem_wb_1_we_out), .A_out(forwarding_1_a_out), .B_out(forwarding_1_b_out));
  EX_MEM ex_mem_1 (
    .Word_in(execute_1_word_out), .CLK(clock_1_out), .C_in(out_4), .rW(execute_1_rw_out),
    .WE_in(execute_1_we_out), .Word_out(ex_mem_1_word_out), .C_out(out_11), .rW_out(out_6),
    .WE_out(ex_mem_1_we_out));
  Memory memory_1 (
    .Word_in(ex_mem_1_word_out), .C_in(out_11), .CLK(clock_1_out), .We_in(ex_mem_1_we_out), .rW(out_6),
    .C_out(memory_1_c_out), .Data(memory_1_data), .WE_OUT(memory_1_we_out), .rW_out(out_9));
  MEM_WB mem_wb_1 (
    .CLK(clock_1_out), .C_in(memory_1_c_out), .Data_in(memory_1_data), .We_in(memory_1_we_out), .rW(out_9),
    .C_out(mem_wb_1_c_out), .Data_out(mem_wb_1_data_out), .We_out(mem_wb_1_we_out), .rW_out(out_8));
  Writeback writeback_1 (
    .C_in(mem_wb_1_c_out), .Data(mem_wb_1_data_out), .WE_in(mem_wb_1_we_out), .rW(out_8), .C_out(out_1),
    .We_out(writeback_1_we_out), .rW_out(writeback_1_rw_out));
endmodule

module Fetch (
  input  CLK,
  output [31:0] Word
);

  wire [1:0] incrementer_1_p3;
  wire [29:0] incrementer_1_p1, incrementer_1_p2;

  // Incrementer #(.width(30)) incrementer_1: pin names not known; wires that end beside it: incrementer_1_p1, incrementer_1_p2, {incrementer_1_p1, incrementer_1_p3}
  Register #(.width(32)) register_1 (
    .D({incrementer_1_p2, incrementer_1_p3}), .en(CLK), .clk(CLK), .Q({incrementer_1_p1, incrementer_1_p3}));  // open: clr
  // MIPSProgramROM mipsprogramrom_1: pin names not known; wires that end beside it: Word

  // Notes on the sheet:
  //   contents of mipsprogramrom_1 (hex, n*v repeats v):
  //   ADDIU $2, $zero, 7411 ADDIU $3, $zero, 22529 ADDIU $4, $zero, 13062 ADDIU $5, $zero, 12397 ADDIU $6,
  //   $zero, 19685 SRLV $7, $4, $1 SLLV $8, $2, $4 SRLV $9, $2, $4 SRAV $10, $3, $2 SRLV $11, $3, $1 SRAV
  //   $12, $3, $3 SRAV $13, $3, $3 SRAV $14, $4, $3 SRLV $15, $2, $3 SLLV $16, $4, $4 SRAV $17, $1, $4
  //   SRAV $18, $4, $3 SLLV $19, $3, $3 SLLV $20, $3, $2 SRLV $21, $2, $1 SLLV $22, $2, $2 SLLV $23, $2,
  //   $1 SRLV $24, $2, $4 SRAV $25, $4, $4 SRLV $26, $4, $1 SRLV $27, $3, $4 SLLV $28, $1, $2 SRAV $29,
  //   $4, $1 SRLV $30, $4, $2 SLLV $31, $2, $4
endmodule

module Decode (
  input  [31:0] C_In,
  input  CLK,
  input  WE_in,
  input  [31:0] Word,
  input  [4:0] rW_in,
  output [31:0] Aout,
  output [31:0] LUI_Data_out,
  output [31:0] B_out,
  output [4:0] Sa_out,
  output [31:0] Ctrl_out,
  output WE,
  output LUI_out,
  output [3:0] Op_ALU_out,
  output SLT_out,
  output SLTU_out,
  output [4:0] rW,
  output [4:0] rA,
  output [4:0] rB
);

  wire controls_1_shift_var, not_1_out;
  wire [4:0] bit_extender_1_out, multiplexer_2_out;
  wire [31:0] bit_extender_3_out, bit_extender_4_out, multiplexer_4_out, registerfile_1_p8;

  not not_1 (not_1_out, CLK);
  assign bit_extender_1_out = {{4{Word[30]}}, Word[30]};  // Bit_Extender bit_extender_1
  Multiplexer #(.width(5), .enable("false")) multiplexer_1 (
    .in0(Word[20:16]), .in1(bit_extender_1_out), .out(rB), .sel(Word[29]));
  assign LUI_Data_out[15:0] = {{15{Word[30]}}, Word[30]};  // Bit_Extender bit_extender_2
  Multiplexer #(.width(5), .enable("false")) multiplexer_2 (
    .in0(Word[15:11]), .in1(Word[20:16]), .out(multiplexer_2_out), .sel(Word[29]));
  assign bit_extender_3_out = {{16{Word[15]}}, Word[15:0]};  // Bit_Extender bit_extender_3
  assign bit_extender_4_out = {{16{1'b0}}, Word[15:0]};  // Bit_Extender bit_extender_4
  Multiplexer #(.width(5), .enable("false")) multiplexer_3 (
    .in0(multiplexer_2_out), .in1(Word[20:16]), .out(rW), .sel(Word[31]));
  Controls controls_1 (
    .Opcode(Word[31:26]), .Funct(Word[5:0]), .WE(WE), .LUI(LUI_out), .Op_ALU(Op_ALU_out), .SLT(SLT_out),
    .SLTU(SLTU_out), .shift_var(controls_1_shift_var));
  // RegisterFile registerfile_1: pin names not known; wires that end beside it: C_In, not_1_out, WE_in, rW_in, Word[25:21], rB, Aout, registerfile_1_p8
  Multiplexer #(.width(32), .enable("false")) multiplexer_4 (
    .in0(bit_extender_3_out), .in1(bit_extender_4_out), .out(multiplexer_4_out), .sel(Word[28]));
  Multiplexer #(.width(32), .enable("false")) multiplexer_5 (
    .in0(registerfile_1_p8), .in1(multiplexer_4_out), .out(B_out), .sel(Word[29]));
  Multiplexer #(.width(5), .enable("false")) multiplexer_6 (
    .in0(Word[10:6]), .in1(Aout[4:0]), .out(Sa_out), .sel(controls_1_shift_var));

  assign Ctrl_out = Word;
  assign LUI_Data_out[31:16] = Word[15:0];
  assign rA = Word[25:21];
endmodule

module Controls (
  input  [5:0] Opcode,
  input  [5:0] Funct,
  output WE,
  output LUI,
  output [3:0] Op_ALU,
  output SLT,
  output SLTU,
  output shift_var
);

  wire and_1_out, and_2_out, and_3_out, and_5_out, and_6_out, and_7_out, and_8_out, nor_1_out, nor_2_out,
       not_1_out, not_3_out, not_4_out, not_7_out, not_8_out, or_1_out;
  wire [2:0] not_5_out;
  wire [3:0] multiplexer_1_out;
  wire [3:3] xor_1_out;

  not not_1 (not_1_out, Funct[5]);
  nor nor_1 (nor_1_out, Opcode[3], Opcode[4], Opcode[5]);
  or or_1 (or_1_out, Opcode[0], Opcode[1], Opcode[2]);
  // NOT_Gate not_2 has open pins: in=Funct[2], out=open
  not not_3 (not_3_out, Funct[5]);
  and and_1 (and_1_out, Funct[2], not_1_out);
  xor xor_1 (xor_1_out[3], and_1_out, Funct[2]);
  nand nand_1 (WE, nor_1_out, or_1_out);
  and and_2 (and_2_out, not_3_out, Funct[0], Funct[1]);
  and and_3 (and_3_out, not_4_out, Funct[3]);
  not not_4 (not_4_out, Funct[2]);
  not not_5 (not_5_out[0], Funct[4]);
  not not_6 (not_5_out[2], Funct[4]);
  and and_4 (LUI, Opcode[0], Opcode[1], Opcode[2]);
  not not_7 (not_7_out, Opcode[2]);
  and and_5 (and_5_out, Opcode[1], not_7_out);
  Multiplexer #(.width(4), .enable("false")) multiplexer_1 (
    .in0({xor_1_out[3], Funct[1:0], Funct[4]}), .in1({Funct[4], not_5_out[2], Funct[4], not_5_out[0]}),
    .out(multiplexer_1_out), .sel(and_2_out));
  nor nor_2 (nor_2_out, Opcode[0], Opcode[1], Opcode[2], Opcode[4], Opcode[5], Opcode[3]);
  Multiplexer #(.width(4), .enable("false")) multiplexer_2 (
    .in0(multiplexer_1_out), .in1({Opcode[2:0], Opcode[5]}), .out(Op_ALU), .sel(Opcode[3]));
  not not_8 (not_8_out, Opcode[3]);
  and and_6 (and_6_out, not_8_out, and_3_out);
  and and_7 (and_7_out, and_5_out, Opcode[0]);
  and and_8 (and_8_out, Funct[0], nor_2_out, and_3_out);
  and and_9 (shift_var, nor_2_out, and_1_out);
  or or_2 (SLT, and_5_out, and_6_out);
  or or_3 (SLTU, and_7_out, and_8_out);

  // Notes on the sheet:
  //   Arith
endmodule

module Execute (
  input  [31:0] A,
  input  [31:0] B,
  input  [31:0] LUI_Data,
  input  LUI,
  input  SLT,
  input  [3:0] Op_ALU,
  input  [4:0] Sa,
  input  SLTU,
  input  [31:0] Word_in,
  input  [4:0] rW,
  input  WE_in,
  output [31:0] C,
  output [31:0] Word_out,
  output [4:0] rW_out,
  output WE_out
);

  wire and_1_out, and_2_out, comparator_1_eq, comparator_1_lt, comparator_2_eq, comparator_2_lt,
       multiplexer_2_out, not_1_out, not_2_out;
  wire [31:0] bit_extender_1_out, mips_alu_1_p5, multiplexer_1_out;

  // Mips_ALU mips_alu_1: pin names not known; wires that end beside it: A, B, Op_ALU, Sa, mips_alu_1_p5
  Comparator #(.width(32)) comparator_1 (.a(A), .b(B), .eq(comparator_1_eq), .lt(comparator_1_lt));  // open: gt
  Comparator #(.width(32), .mode("unsigned")) comparator_2 (
    .a(A), .b(B), .eq(comparator_2_eq), .lt(comparator_2_lt));  // open: gt
  not not_1 (not_1_out, comparator_1_eq);
  not not_2 (not_2_out, comparator_2_eq);
  Multiplexer #(.width(32), .enable("false")) multiplexer_1 (
    .in0(mips_alu_1_p5), .in1(LUI_Data), .out(multiplexer_1_out), .sel(LUI));
  and and_1 (and_1_out, not_1_out, comparator_1_lt);
  and and_2 (and_2_out, not_2_out, comparator_2_lt);
  Multiplexer #(.enable("false")) multiplexer_2 (.in0(and_1_out), .in1(and_2_out), .out(multiplexer_2_out), .sel(SLTU));
  Multiplexer #(.width(32), .enable("false")) multiplexer_3 (
    .in0(multiplexer_1_out), .in1(bit_extender_1_out), .out(C), .sel(SLT));
  assign bit_extender_1_out = {{31{1'b0}}, multiplexer_2_out};  // Bit_Extender bit_extender_1

  assign rW_out = rW;
  assign WE_out = WE_in;
  assign Word_out = Word_in;

  // Notes on the sheet:
  //   SLT
  //   SLTU
endmodule

module Memory (
  input  [31:0] Word_in,
  input  [31:0] C_in,
  input  CLK,
  input  We_in,
  input  [4:0] rW,
  output [31:0] C_out,
  output [31:0] Data,
  output WE_OUT,
  output [4:0] rW_out
);

  // LCD_Video lcd_video_1: pin names not known; wires that end beside it: CLK, CLK

  assign C_out = C_in;
  assign Data = C_in;
  assign rW_out = rW;
  assign WE_OUT = We_in;
endmodule

module Writeback (
  input  [31:0] C_in,
  input  [31:0] Data,
  input  WE_in,
  input  [4:0] rW,
  output [31:0] C_out,
  output We_out,
  output [4:0] rW_out
);

  Multiplexer #(.width(32), .enable("false")) multiplexer_1 (.in0(C_in), .in1(Data), .out(C_out), .sel(WE_in));

  assign rW_out = rW;
  assign We_out = WE_in;
endmodule

module ID_EX (
  input  [31:0] A_in,
  input  [31:0] LUI_Data_in,
  input  [31:0] B_in,
  input  CLK,
  input  [4:0] Sa_in,
  input  SLT_in,
  input  SLTU_in,
  input  LUI_in,
  input  [31:0] Ctrl_in,
  input  [3:0] Op_ALU_in,
  input  [4:0] rW_in,
  input  [4:0] rA,
  input  [4:0] rB,
  input  WE,
  output [31:0] A_out,
  output [31:0] LUI_Data_out,
  output [31:0] B_out,
  output [4:0] Sa_out,
  output SLT_out,
  output SLTU_out,
  output LUI_out,
  output [31:0] Ctrl_out,
  output [3:0] Op_ALU_out,
  output [4:0] rW_out,
  output [4:0] rA_out,
  output [4:0] rB_out,
  output WE_out
);

  Register #(.width(32)) A_reg (.D(A_in), .en(CLK), .clk(CLK), .Q(A_out));  // open: clr
  Register #(.width(32)) LUI_Data_reg (.D(LUI_Data_in), .en(CLK), .clk(CLK), .Q(LUI_Data_out));  // open: clr
  Register #(.width(32)) B_reg (.D(B_in), .en(CLK), .clk(CLK), .Q(B_out));  // open: clr
  Register #(.width(5)) Sa_reg (.D(Sa_in), .en(CLK), .clk(CLK), .Q(Sa_out));  // open: clr
  Register #(.width(1)) SLTU_reg (.D(SLTU_in), .en(CLK), .clk(CLK), .Q(SLTU_out));  // open: clr
  Register #(.width(1)) LUI_reg (.D(LUI_in), .en(CLK), .clk(CLK), .Q(LUI_out));  // open: clr
  Register #(.width(32)) Ctrl_reg (.D(Ctrl_in), .en(CLK), .clk(CLK), .Q(Ctrl_out));  // open: clr
  Register #(.width(4)) Op_ALU_reg (.D(Op_ALU_in), .en(CLK), .clk(CLK), .Q(Op_ALU_out));  // open: clr
  Register #(.width(5)) register_1 (.D(rW_in), .en(CLK), .clk(CLK), .Q(rW_out));  // open: clr
  Register #(.width(5)) register_2 (.D(rA), .en(CLK), .clk(CLK), .Q(rA_out));  // open: clr
  Register #(.width(5)) register_3 (.D(rB), .en(CLK), .clk(CLK), .Q(rB_out));  // open: clr
  Register #(.width(1)) register_4 (.D(WE), .en(CLK), .clk(CLK), .Q(WE_out));  // open: clr
  Register #(.width(1)) SLT_reg (.D(SLT_in), .en(CLK), .clk(CLK), .Q(SLT_out));  // open: clr
endmodule

module IF_ID (
  input  [31:0] Word_in,
  input  CLK,
  output [31:0] Word_out
);

  Register #(.width(32)) register_1 (.D(Word_in), .en(CLK), .clk(CLK), .Q(Word_out));  // open: clr
endmodule

module EX_MEM (
  input  [31:0] Word_in,
  input  CLK,
  input  [31:0] C_in,
  input  [4:0] rW,
  input  WE_in,
  output [31:0] Word_out,
  output [31:0] C_out,
  output [4:0] rW_out,
  output WE_out
);

  Register #(.width(32)) register_1 (.D(Word_in), .en(CLK), .clk(CLK), .Q(Word_out));  // open: clr
  Register #(.width(32)) register_2 (.D(C_in), .en(CLK), .clk(CLK), .Q(C_out));  // open: clr
  Register #(.width(5)) register_3 (.D(rW), .en(CLK), .clk(CLK), .Q(rW_out));  // open: clr
  Register #(.width(1)) register_4 (.D(WE_in), .en(CLK), .clk(CLK), .Q(WE_out));  // open: clr
endmodule

module MEM_WB (
  input  CLK,
  input  [31:0] C_in,
  input  [31:0] Data_in,
  input  We_in,
  input  [4:0] rW,
  output [31:0] C_out,
  output [31:0] Data_out,
  output We_out,
  output [4:0] rW_out
);

  Register #(.width(32)) register_1 (.D(C_in), .en(CLK), .clk(CLK), .Q(C_out));  // open: clr
  Register #(.width(32)) register_2 (.D(Data_in), .en(CLK), .clk(CLK), .Q(Data_out));  // open: clr
  Register #(.width(1)) register_3 (.D(We_in), .en(CLK), .clk(CLK), .Q(We_out));  // open: clr
  Register #(.width(5)) register_4 (.D(rW), .en(CLK), .clk(CLK), .Q(rW_out));  // open: clr
endmodule

module Forwarding (
  input  [31:0] ID_EX_A,
  input  [31:0] ID_EX_B,
  input  [31:0] EX_MEM_Out,
  input  [31:0] MEM_WB_Out,
  input  [4:0] rA,
  input  [4:0] rB,
  input  [4:0] rD_EX_MEM,
  input  [4:0] rD_MEM_WB,
  input  WE_EX_MEM,
  input  WE_MEM_WB,
  output [31:0] A_out,
  output [31:0] B_out
);

  wire and_1_out, and_2_out, and_3_out, and_4_out, checknot0_1_aout, checknot0_2_aout, checknot0_3_aout,
       checknot0_4_aout, checknot0_5_aout, checknot0_6_aout, not_1_out, not_2_out, not_3_out, not_4_out;
  wire [4:0] xor_1_out, xor_2_out, xor_3_out, xor_4_out;
  wire [31:0] multiplexer_1_out, multiplexer_3_out;

  assign xor_1_out = rA ^ rD_EX_MEM;  // XOR_Gate xor_1, 5 bits wide
  assign xor_2_out = rB ^ rD_EX_MEM;  // XOR_Gate xor_2, 5 bits wide
  assign xor_3_out = rA ^ rD_MEM_WB;  // XOR_Gate xor_3, 5 bits wide
  assign xor_4_out = rB ^ rD_MEM_WB;  // XOR_Gate xor_4, 5 bits wide
  not not_1 (not_1_out, checknot0_1_aout);
  CheckNot0 checknot0_1 (.Ain(xor_1_out), .Aout(checknot0_1_aout));
  not not_2 (not_2_out, checknot0_2_aout);
  CheckNot0 checknot0_2 (.Ain(xor_2_out), .Aout(checknot0_2_aout));
  CheckNot0 checknot0_3 (.Ain(rD_EX_MEM), .Aout(checknot0_3_aout));
  not not_3 (not_3_out, checknot0_4_aout);
  CheckNot0 checknot0_4 (.Ain(xor_3_out), .Aout(checknot0_4_aout));
  not not_4 (not_4_out, checknot0_5_aout);
  CheckNot0 checknot0_5 (.Ain(xor_4_out), .Aout(checknot0_5_aout));
  CheckNot0 checknot0_6 (.Ain(rD_MEM_WB), .Aout(checknot0_6_aout));
  Multiplexer #(.width(32), .enable("false")) multiplexer_1 (
    .in0(ID_EX_A), .in1(MEM_WB_Out), .out(multiplexer_1_out), .sel(and_3_out));
  and and_1 (and_1_out, not_1_out, WE_EX_MEM, checknot0_3_aout);
  and and_2 (and_2_out, not_2_out, WE_EX_MEM, checknot0_3_aout);
  and and_3 (and_3_out, not_3_out, WE_MEM_WB, checknot0_6_aout);
  and and_4 (and_4_out, not_4_out, WE_MEM_WB, checknot0_6_aout);
  Multiplexer #(.width(32), .enable("false")) multiplexer_2 (
    .in0(multiplexer_1_out), .in1(EX_MEM_Out), .out(A_out), .sel(and_1_out));
  Multiplexer #(.width(32), .enable("false")) multiplexer_3 (
    .in0(ID_EX_B), .in1(MEM_WB_Out), .out(multiplexer_3_out), .sel(and_4_out));
  Multiplexer #(.width(32), .enable("false")) multiplexer_4 (
    .in0(multiplexer_3_out), .in1(EX_MEM_Out), .out(B_out), .sel(and_2_out));
endmodule

module CheckNot0 (
  input  [4:0] Ain,
  output Aout
);

  or or_1 (Aout, Ain[0], Ain[1], Ain[2], Ain[3], Ain[4]);
endmodule
